# Fritzing sketch circuit (saved by Fritzing 0.9.3b)
circuit board: 8.46667cm x 5.64444cm
breadboards: 1

parts:
  part = Arduino Nano (Rev3.0) (ICSP)
  part_2 = Sharp PC817 [package=THT]
  part_3 = Sharp PC817 [package=THT]
  R1 = Resistor [tolerance=±0.05% resistance=10k package="0402 [SMD]"]
  R2 = Resistor [tolerance=±0.05% resistance=10k package="0402 [SMD]"]
  R3 = Resistor [tolerance=±0.05% resistance=1k package="0402 [SMD]"]
  R4 = Resistor [tolerance=±0.05% resistance=1k package="0402 [SMD]"]
  J1 = male pin header, 5 pins [form="♂ (male)"]
  R5 = Resistor [tolerance=±0.05% resistance=10k package="0402 [SMD]"]
  R6 = Resistor [tolerance=±0.05% resistance=10k package="0402 [SMD]"]

nets:
  GND: part.GND, part.D10, part_2.Pin_2, part_2.Pin_3, part_3.Pin_2, part_3.Pin_3, R1.Pin_1, R2.Pin_1, J1.pin4
  N1: part.D2, R1.Pin_0, R3.Pin_1
  N2: part.D3, R2.Pin_0, R4.Pin_1
  N3: part.D11/MOSI, J1.pin2
  N4: part.5V, J1.pin5
  N5: part.D13/SCK, J1.pin1
  N6: part_2.Pin_1, R3.Pin_0
  N7: part_2.Pin_4, R5.Pin_1
  N8: part_3.Pin_1, R4.Pin_0
  N9: part_3.Pin_4, R6.Pin_1
  N10: J1.pin3, R5.Pin_0, R6.Pin_0

notes:
  clock
  data
  gnd
  +5v
  buttons
