# Fritzing sketch circuit (saved by Fritzing 0.9.3b)
circuit board: 8.46667cm x 5.64444cm
perfboards: 1

parts:
  Part1 = Arduino Nano (Rev3.0) (ICSP)
  U1 = Sharp PC817 [part_number="управление режимом" package=THT]
  U2 = Sharp PC817 [part_number="управление сбросом" package=THT]
  R1 = Resistor [tolerance=±0.05% resistance=10k package="0402 [SMD]"]
  R2 = Resistor [tolerance=±0.05% resistance=10k package="0402 [SMD]"]
  R3 = Resistor [tolerance=±0.05% resistance=1k package="0402 [SMD]"]
  R4 = Resistor [tolerance=±0.05% resistance=1k package="0402 [SMD]"]
  R5 = Resistor [tolerance=±0.05% resistance=6.8k part_number=режим package="0402 [SMD]"]
  R6 = Resistor [tolerance=±0.05% resistance=5k part_number=сброс package="0402 [SMD]"]
  IC1 = SO08 [chip_label=L9637 package=SO]
  J1 = male pin header, 7 pins [form="♂ (male)"]
  R7 = Resistor [tolerance=±0.05% resistance=510 package="0402 [SMD]"]

nets:
  GND: Part1.GND, Part1.D10, U1.Pin_2, U1.Pin_3, U2.Pin_2, U2.Pin_3, R1.Pin_1, R2.Pin_1, IC1.5, J1.pin6
  N1: Part1.D2, R1.Pin_0, R3.Pin_1
  N2: Part1.D3, R2.Pin_0, R4.Pin_1
  N3: Part1.D4, IC1.1
  N4: Part1.D5, IC1.4
  N5: Part1.D11/MOSI, J1.pin4
  N6: Part1.5V, IC1.3, J1.pin7
  N7: Part1.D13/SCK, J1.pin3
  N8: U1.Pin_1, R3.Pin_0
  N9: U1.Pin_4, R5.Pin_1
  N10: U2.Pin_1, R4.Pin_0
  N11: U2.Pin_4, R6.Pin_1
  N12: R5.Pin_0, R6.Pin_0, J1.pin5
  N13: IC1.6, J1.pin2, R7.Pin_1
  N14: IC1.7, J1.pin1, R7.Pin_0

notes:
  clock
  data
  gnd
  +5v
  buttons
  - R1, R2 - подтягивают цифровые выходы на землю, для предотвращения появления на них высокого уровня, при подаче питания / перезагрузке
  - R3, R4 - нужны для того чтобы не сгорел диод в оптопаре, номинал нужно подобрать в зависимости от используемой оптопары
  - U1, U2 - оптопары для программного нажатия на кнопки сброса и режима, подойдут любые, я использовал одну сдвоенную
  - R5, R6 - резисторы для программного нажатия на кнопки сброса и режима, нужно подобрать что нибудь +/- близкое
  K-Line
  +12v
